# Fritzing sketch MObject (saved by Fritzing 0.6.3b)
breadboards: 2

parts:
  U1 = 3-Axis Accelerometer Breakout
  U2 = LM 358 Dual Op-Amp [package="DIP8 [THT]"]
  R2 = Resistor [tolerance=±5% resistance=100k package=THT]
  R3 = Resistor [tolerance=±5% resistance=100k package=THT]
  R4 = Resistor [tolerance=±5% resistance=100k package=THT]
  R5 = Resistor [tolerance=±5% resistance=100k package=THT]
  R6 = Resistor [tolerance=±5% resistance=100k package=THT]
  R7 = Resistor [tolerance=±5% resistance=100k package=THT]
  R8 = Resistor [tolerance=±5% resistance=100k package=THT]
  R9 = Resistor [tolerance=±5% resistance=220 package=THT]
  R10 = Resistor [tolerance=±5% resistance=220 package=THT]
  R11 = Resistor [tolerance=±5% resistance=220 package=THT]
  R12 = Resistor [tolerance=±5% resistance=220 package=THT]
  R13 = Resistor [tolerance=±5% resistance=220 package=THT]
  R14 = Resistor [tolerance=±5% resistance=220 package=THT]
  R15 = Resistor [tolerance=±5% resistance=220 package=THT]
  R16 = Resistor [tolerance=±5% resistance=220 package=THT]
  R17 = Resistor [tolerance=±5% resistance=100k package=THT]
  C1 = Ceramic Capacitor [capacitance=10nF package="100 mil [THT, multilayer]"]
  R18 = Resistor [tolerance=±5% resistance=100k package=THT]
  R19 = Resistor [tolerance=±5% resistance=100k package=THT]
  R20 = Resistor [tolerance=±5% resistance=100k package=THT]
  R21 = Resistor [tolerance=±5% resistance=100k package=THT]
  R22 = Resistor [tolerance=±5% resistance=100k package=THT]
  R23 = Resistor [tolerance=±5% resistance=100k package=THT]
  R24 = Resistor [tolerance=±5% resistance=100k package=THT]
  LED1 = LED - 5mm [color="Red (635nm)" package="5 mm [THT]"]
  R25 = Resistor [tolerance=±5% resistance=1k package=THT]
  R26 = Resistor [tolerance=±5% resistance=1k package=THT]
  R27 = Resistor [tolerance=±5% resistance=1k package=THT]
  R28 = Resistor [tolerance=±5% resistance=1k package=THT]
  R29 = Resistor [tolerance=±5% resistance=1k package=THT]
  LED2 = LED - 5mm [color="Red (635nm)" package="5 mm [THT]"]
  LED3 = LED - 5mm [color="Red (635nm)" package="5 mm [THT]"]
  LED4 = LED - 5mm [color="Red (635nm)" package="5 mm [THT]"]
  LED5 = LED - 5mm [color="Yellow (592nm)" package="5 mm [THT]"]
  MIC1 = Microphone
  R30 = Resistor [tolerance=±5% resistance=10k package=THT]
  R31 = Resistor [tolerance=±5% resistance=10k package=THT]
  SPKR1 = Loudspeaker
  R32 = Resistor [tolerance=±5% resistance=33k package=THT]
  J1 = female pin header, 15 pins [form="♀ (female)"]
  J2 = female pin header, 15 pins [form="♀ (female)"]
  R1 = Resistor [tolerance=±5% resistance=100k package=THT]

nets:
  N1: U1.Z, J1.pin9
  N2: U1.Y, J1.pin10
  N3: U1.X, J1.pin11
  N4: U1.GND, U2.connector3, R24.Pin_1, R25.Pin_0, R26.Pin_0, R27.Pin_0, R28.Pin_0, R29.Pin_0, MIC1.pin2, R31.Pin_1, SPKR1.pin1, J1.pin14
  N5: U1.VDD, U2.connector7, J1.pin12
  N6: U2.connector0, U2.connector1, U2.connector4
  N7: U2.connector2, R9.Pin_0, R17.Pin_1
  N8: U2.connector5, R30.Pin_0, R31.Pin_0
  N9: U2.connector6, C1.0, R30.Pin_1
  N10: R2.Pin_0, R11.Pin_1
  N11: R2.Pin_1, J2.pin8
  N12: R3.Pin_0, R13.Pin_1
  N13: R3.Pin_1, J2.pin10
  N14: R4.Pin_0, R10.Pin_1
  N15: R4.Pin_1, J2.pin7
  N16: R5.Pin_0, R12.Pin_1
  N17: R5.Pin_1, J2.pin9
  N18: R6.Pin_0, R14.Pin_1
  N19: R6.Pin_1, J2.pin11
  N20: R7.Pin_0, R15.Pin_1
  N21: R7.Pin_1, J2.pin14
  N22: R8.Pin_0, R16.Pin_1
  N23: R8.Pin_1, J2.pin15
  N24: R9.Pin_1, R1.Pin_0
  N25: R10.Pin_0, R17.Pin_0, R18.Pin_1
  N26: R11.Pin_0, R18.Pin_0, R19.Pin_1
  N27: R12.Pin_0, R19.Pin_0, R20.Pin_1
  N28: R13.Pin_0, R20.Pin_0, R21.Pin_1
  N29: R14.Pin_0, R21.Pin_0, R22.Pin_1
  N30: R15.Pin_0, R23.Pin_1, R24.Pin_0
  N31: R16.Pin_0, R22.Pin_0, R23.Pin_0
  N32: C1.1, R32.Pin_1
  N33: LED1.cathode, R29.Pin_1
  N34: LED1.anode, J2.pin5
  N35: R25.Pin_1, LED5.cathode
  N36: R26.Pin_1, LED4.cathode
  N37: R27.Pin_1, LED2.cathode
  N38: R28.Pin_1, LED3.cathode
  N39: LED2.anode, J2.pin4
  N40: LED3.anode, J2.pin3
  N41: LED4.anode, J2.pin2
  N42: LED5.anode, J2.pin1
  N43: MIC1.pin1, J1.pin8
  N44: SPKR1.pin2, R32.Pin_0
  N45: J2.pin6, R1.Pin_1
